# Fritzing sketch LM358synth (saved by Fritzing 0.9.3b)
breadboards: 1

parts:
  IC1 = IC, DIP package, 8 pins [chip_label=IC]
  R4 = Resistor [tolerance=±5% resistance=100k package=THT]
  VCC1 = Battery block 9V
  R5 = Resistor [tolerance=±5% resistance=100k package=THT]
  R1 = Resistor [tolerance=±5% resistance=47k package=THT]
  R2 = Resistor [tolerance=±5% resistance=22k package=THT]
  S1 = Momentary Switch [package=ksa_sealed_tac_switch]
  R6 = Rotary Potentiometer (Small) [maximum_resistance=100kΩ package=THT]
  R3 = Resistor [tolerance=±5% resistance=10k package=THT]
  C1 = Ceramic Capacitor [capacitance=100nF package="100 mil [THT, multilayer]"]
  IC3 = IC, DIP package, 8 pins [chip_label=LM358]
  IC4 = IC, DIP package, 8 pins [chip_label=IC]
  C2 = Electrolytic Capacitor [capacitance=1µF package="100 mil [THT, electrolytic]"]
  R7 = Resistor [tolerance=±5% resistance=22k package=THT]
  R9 = Resistor [tolerance=±5% resistance=47k package=THT]
  R10 = Resistor [tolerance=±5% resistance=220 package=THT]
  R11 = Resistor [tolerance=±5% resistance=100k package=THT]  # not connected
  R12 = Resistor [tolerance=±5% resistance=100k package=THT]

nets:
  N1: IC1.pin1, R1.Pin_1, S1.2
  N2: IC1.pin2, IC1.pin5, R4.Pin_0, R5.Pin_1
  N3: IC1.pin3, R1.Pin_0, R2.Pin_0
  N4: IC1.pin4, R4.Pin_1, VCC1.-, R6.leg1, R12.Pin_1
  N5: IC1.pin6, R3.Pin_0, C1.1
  N6: IC1.pin7, R2.Pin_1, C1.0, IC3.pin2
  N7: IC1.pin8, VCC1.+, R5.Pin_0, IC4.pin8
  N8: S1.1, R6.wiper
  N9: R6.leg2, R3.Pin_1
  N10: IC4.pin1, R9.Pin_1, R10.Pin_1
  N11: IC4.pin2, IC4.pin5, R12.Pin_0
  N12: IC4.pin3, R7.Pin_0, R9.Pin_0
  N13: IC4.pin6, C2.+, R10.Pin_0
  N14: IC4.pin7, C2.-, R7.Pin_1
